# Fritzing sketch unipi (saved by Fritzing 0.9.3b)
breadboards: 1

parts:
  Raspberry_Pi_1 = Raspberry Pi 3 [part_number=RPI-3-V1.2]
  R1 = Rotary Potentiometer (Large) [maximum_resistance=100kΩ package=THT]
  LCD1 = LCD screen
  S1 = Pushbutton [package="[THT]"]
  S2 = Pushbutton [package="[THT]"]
  S3 = Pushbutton [package="[THT]"]
  Part1 = Coin Acceptor - 6-Coin version

nets:
  N1: Raspberry_Pi_1.GPIO3, S2.Pin_3, S2.Pin_4
  N2: Raspberry_Pi_1.GIPO17, Part1.SIG
  N3: Raspberry_Pi_1.GIPO27, LCD1.DB7
  N4: Raspberry_Pi_1.GIPO22, LCD1.DB6
  N5: Raspberry_Pi_1.GIPO19, LCD1.E
  N6: Raspberry_Pi_1.GIPO26, LCD1.RS
  N7: Raspberry_Pi_1.GIPO25, LCD1.DB4
  GND: Raspberry_Pi_1.GND, R1.leg1, LCD1.R/W, LCD1.LED-, S1.Pin_1, S1.Pin_2, S2.Pin_1, S2.Pin_2, Part1.GND
  N8: Raspberry_Pi_1.GIPO24, LCD1.DB5
  5V: Raspberry_Pi_1.5V, R1.leg2, LCD1.VDD, LCD1.LED+
  N9: R1.wiper, LCD1.V0
  N10: S1.Pin_3, S1.Pin_4
  N11: S3.Pin_1, S3.Pin_2
  N12: S3.Pin_3, S3.Pin_4

custom parts:
  Coin Acceptor - 6-Coin version: 12V coin acceptor that can handle up to 6 different denominations. Output is either pulse width, serial, or single pin per coin value.
